# Fritzing sketch wemos_watering_system (saved by Fritzing 0.9.3b)
breadboards: 1

parts:
  U2 = TRANSISTOR_NPN_2 [package=to-92]
  R1 = Resistor [tolerance=±5% resistance=10k package=THT]
  Part3 = Soil Moisture Sensor
  YL-83_-_Control_Board1 = YL-83 Rain Sensor - Control Board
  U3 = TRANSISTOR_NPN_2 [package=to-92]
  R3 = Resistor [tolerance=±5% resistance=10k package=THT]
  WeMos_D1_R1 = WeMos D1 R2
  M1 = DC Motor
  VCC1 = Battery block 9V
  U5 = RELAY [package=relay-jzc]
  Part4 = BME280 Breakout

nets:
  N1: U2.C, YL-83_-_Control_Board1.GND
  N2: U2.B, R1.Pin_0
  GND: U2.E, U3.E, WeMos_D1_R1.GND, Part4.GND
  N3: R1.Pin_1, WeMos_D1_R1.(D6)
  N4: Part3.GND, YL-83_-_Control_Board1.NEG
  N5: Part3.VCC, YL-83_-_Control_Board1.POS
  VCC: YL-83_-_Control_Board1.VCC, WeMos_D1_R1.5V, U5.COIL2
  N6: YL-83_-_Control_Board1.AO, WeMos_D1_R1.A0
  N7: U3.C, U5.COIL1
  N8: U3.B, R3.Pin_0
  N9: R3.Pin_1, WeMos_D1_R1.(D5)
  N10: WeMos_D1_R1.D0/RX, WeMos_D1_R1.RESET
  N11: WeMos_D1_R1.D14, Part4.SDI/SDA
  N12: WeMos_D1_R1.D15, Part4.SCK/SCL
  3.3V: WeMos_D1_R1.3.3V, Part4.3.3V
  N13: M1.pin_1, U5.MAIN
  N14: M1.pin_2, VCC1.-
  N15: VCC1.+, U5.NO

notes:
  D0 and RST are connected to enabling deep sleep mode.
  You have to remove the connection temporarily for flashing firmware.

custom parts:
  YL-83 Rain Sensor - Control Board: The YL-83 is a rain sensor that has more resistance when dry and less resistance when wet. The module runs at 5V.
  WeMos D1 R2: The D1 R2 is a mini wifi board based on the ESP-8266EX.
